# Fritzing sketch DiceBox (saved by Fritzing 1.0.6)

parts:
  Part1 = Arduino Leonardo (Rev3b)
  9V_Battery = Battery Holders [package=battery-aa]
  GY1 = MPU-6050 Board GY-521 [form="♀ (female)" package=THT]
  WS2812B-64_8x8 = ws2812b [package="smd 2812b"]

nets:
  N1: Part1.D2/SDA, GY1.pin8
  N2: Part1.D3_PWM/SCL, Part1.SCL, WS2812B-64_8x8.DIN
  N3: Part1.3V3, GY1.pin1
  5V: Part1.5V, WS2812B-64_8x8.VDD
  GND: Part1.GND, 9V_Battery.+, GY1.pin2, GY1.pin7, WS2812B-64_8x8.VSS
  N4: Part1.VIN, 9V_Battery.-
  N5: Part1.A4, GY1.pin4
  N6: Part1.A5, GY1.pin3

custom parts:
  MPU-6050 Board GY-521: Acelerometro y Giroscopio MPU-6050 Board GY-521
